# Fritzing sketch FanController (saved by Fritzing 0.9.5d)
breadboards: 1

parts:
  Part1 = Arduino Uno (Rev3)
  M1 = DC Motor
  D1 = P1000K [part_number=P1000K]
  Q1 = Basic FET P-Channel [package="DPak [SMD]"]
  S1 = Momentary Switch [package=ksa_sealed_tac_switch]

nets:
  N1: Part1.D13/SCK, S1.3
  N2: Part1.D3_PWM, Q1.Gate
  N3: Part1.5V, D1.cathode
  N4: Part1.GND, M1.pin_2, Q1.source, S1.1
  N5: M1.pin_1, D1.anode, Q1.drain
